// Logisim project LogisimCircuit.circ as structural Verilog
// IR
module _16bit_Register (
  input  Clock,
  input  WE,
  input  [15:0] Input,
  output [15:0] Output
);

  // Probe on Input
  D_Flip_Flop d_ff_1 (.clk(Clock), .D(Input[0]), .Q(Output[0]), .en(WE));  // open: Qn, preset, reset
  D_Flip_Flop d_ff_2 (.clk(Clock), .D(Input[1]), .Q(Output[1]), .en(WE));  // open: Qn, preset, reset
  D_Flip_Flop d_ff_3 (.clk(Clock), .D(Input[2]), .Q(Output[2]), .en(WE));  // open: Qn, preset, reset
  D_Flip_Flop d_ff_4 (.clk(Clock), .D(Input[3]), .Q(Output[3]), .en(WE));  // open: Qn, preset, reset
  D_Flip_Flop d_ff_5 (.clk(Clock), .D(Input[4]), .Q(Output[4]), .en(WE));  // open: Qn, preset, reset
  D_Flip_Flop d_ff_6 (.clk(Clock), .D(Input[5]), .Q(Output[5]), .en(WE));  // open: Qn, preset, reset
  D_Flip_Flop d_ff_7 (.clk(Clock), .D(Input[6]), .Q(Output[6]), .en(WE));  // open: Qn, preset, reset
  D_Flip_Flop d_ff_8 (.clk(Clock), .D(Input[7]), .Q(Output[7]), .en(WE));  // open: Qn, preset, reset
  D_Flip_Flop d_ff_9 (.clk(Clock), .D(Input[8]), .Q(Output[8]), .en(WE));  // open: Qn, preset, reset
  D_Flip_Flop d_ff_10 (.clk(Clock), .D(Input[9]), .Q(Output[9]), .en(WE));  // open: Qn, preset, reset
  D_Flip_Flop d_ff_11 (.clk(Clock), .D(Input[10]), .Q(Output[10]), .en(WE));  // open: Qn, preset, reset
  D_Flip_Flop d_ff_12 (.clk(Clock), .D(Input[11]), .Q(Output[11]), .en(WE));  // open: Qn, preset, reset
  D_Flip_Flop d_ff_13 (.clk(Clock), .D(Input[12]), .Q(Output[12]), .en(WE));  // open: Qn, preset, reset
  D_Flip_Flop d_ff_14 (.clk(Clock), .D(Input[13]), .Q(Output[13]), .en(WE));  // open: Qn, preset, reset
  D_Flip_Flop d_ff_15 (.clk(Clock), .D(Input[14]), .Q(Output[14]), .en(WE));  // open: Qn, preset, reset
  D_Flip_Flop d_ff_16 (.clk(Clock), .D(Input[15]), .Q(Output[15]), .en(WE));  // open: Qn, preset, reset
  // Probe on Output
endmodule

module Regbank (
  input  [15:0] Data_in,
  input  [2:0] Data_Address,
  input  [2:0] Source1,
  input  [2:0] Source2,
  input  clk,
  input  Load,
  input  spinc,
  input  spdec,
  output [15:0] Source1_Out,
  output [15:0] Source2_Out,
  output [15:0] SP_ADDR
);

  wire and_1_out, and_2_out, and_3_out, and_4_out, and_5_out, and_6_out, and_7_out, and_8_out,
       decoder_1_out0, decoder_1_out1, decoder_1_out2, decoder_1_out3, decoder_1_out4, decoder_1_out5,
       decoder_1_out6, decoder_1_out7, or_1_out, or_2_out;
  wire [15:0] adder_1_out, multiplexer_1_out, multiplexer_4_out, n16bit_register_1_output,
       n16bit_register_2_output, n16bit_register_3_output, n16bit_register_4_output,
       n16bit_register_5_output, n16bit_register_6_output, n16bit_register_7_output;

  Decoder #(.select(3)) decoder_1 (
    .out0(decoder_1_out0), .out1(decoder_1_out1), .out2(decoder_1_out2), .out3(decoder_1_out3),
    .out4(decoder_1_out4), .out5(decoder_1_out5), .out6(decoder_1_out6), .out7(decoder_1_out7),
    .sel(Data_Address));  // open: en
  and and_1 (and_1_out, Load, decoder_1_out0);
  and and_2 (and_2_out, Load, decoder_1_out1);
  and and_3 (and_3_out, Load, decoder_1_out2);
  and and_4 (and_4_out, Load, decoder_1_out3);
  and and_5 (and_5_out, Load, decoder_1_out4);
  and and_6 (and_6_out, Load, decoder_1_out5);
  and and_7 (and_7_out, Load, decoder_1_out6);
  and and_8 (and_8_out, Load, decoder_1_out7);
  _16bit_Register u_16bit_register_1 (.Clock(clk), .WE(and_2_out), .Input(Data_in), .Output(n16bit_register_1_output));
  _16bit_Register u_16bit_register_2 (.Clock(clk), .WE(and_3_out), .Input(Data_in), .Output(n16bit_register_2_output));
  _16bit_Register u_16bit_register_3 (.Clock(clk), .WE(and_4_out), .Input(Data_in), .Output(n16bit_register_3_output));
  _16bit_Register u_16bit_register_4 (.Clock(clk), .WE(and_5_out), .Input(Data_in), .Output(n16bit_register_4_output));
  _16bit_Register u_16bit_register_5 (.Clock(clk), .WE(and_6_out), .Input(Data_in), .Output(n16bit_register_5_output));
  _16bit_Register u_16bit_register_6 (.Clock(clk), .WE(and_7_out), .Input(Data_in), .Output(n16bit_register_6_output));
  _16bit_Register u_16bit_register_7 (.Clock(clk), .WE(and_1_out), .Input(Data_in), .Output(n16bit_register_7_output));
  Multiplexer #(.select(2), .width(16)) multiplexer_1 (
    .in1(16'h1), .in2({16{1'b1}}), .out(multiplexer_1_out), .sel({spdec, spinc}));  // open: in0, in3, en
  Adder #(.width(16)) adder_1 (.a(multiplexer_1_out), .b(SP_ADDR), .out(adder_1_out));  // open: cin, cout
  Multiplexer #(.select(3), .width(16)) multiplexer_2 (
    .in0(n16bit_register_7_output), .in1(n16bit_register_1_output), .in2(n16bit_register_2_output),
    .in3(n16bit_register_3_output), .in4(n16bit_register_4_output), .in5(n16bit_register_5_output),
    .in6(n16bit_register_6_output), .in7(SP_ADDR), .out(Source1_Out), .sel(Source1));  // open: en
  Multiplexer #(.select(3), .width(16)) multiplexer_3 (
    .in0(n16bit_register_7_output), .in1(n16bit_register_1_output), .in2(n16bit_register_2_output),
    .in3(n16bit_register_3_output), .in4(n16bit_register_4_output), .in5(n16bit_register_5_output),
    .in6(n16bit_register_6_output), .in7(SP_ADDR), .out(Source2_Out), .sel(Source2));  // open: en
  or or_1 (or_1_out, and_8_out, or_2_out);
  or or_2 (or_2_out, spinc, spdec);
  Multiplexer #(.width(16)) multiplexer_4 (
    .in0(adder_1_out), .in1(Data_in), .out(multiplexer_4_out), .sel(Load));  // open: en
  Register #(.width(16)) register_1 (.D(multiplexer_4_out), .en(or_1_out), .Q(SP_ADDR), .clk(clk));  // open: clr

  // Other names for the same wires on the sheet: ld = Load
endmodule

module ALU (
  input  [15:0] Left,
  input  [15:0] Right,
  input  zfld,
  input  clk,
  input  [2:0] Alu_Op,
  input  [2:0] scr1,
  output ZF,
  output [15:0] Alu_result
);

  wire comparator_1_eq;
  wire [15:0] adder_1_out, adder_2_out, and_1_out, multiplexer_2_out, not_1_out, or_1_out, subtractor_1_out,
       subtractor_2_out, xor_1_out;

  Adder #(.width(16)) adder_1 (.a(Left), .b(Right), .out(adder_1_out));  // open: cin, cout
  Subtractor #(.width(16)) subtractor_1 (.a(Left), .b(Right), .out(subtractor_1_out));  // open: bin, bout
  assign and_1_out = Left & Right;  // AND_Gate and_1, 16 bits wide
  assign or_1_out = Left | Right;  // OR_Gate or_1, 16 bits wide
  assign xor_1_out = Left ^ Right;  // XOR_Gate xor_1, 16 bits wide
  assign not_1_out = ~Right;  // NOT_Gate not_1, 16 bits wide
  Adder #(.width(16)) adder_2 (.a(16'h1), .b(Right), .out(adder_2_out));  // open: cin, cout
  Subtractor #(.width(16)) subtractor_2 (.a(Right), .b(16'h1), .out(subtractor_2_out));  // open: bin, bout
  Multiplexer #(.select(3), .width(16)) multiplexer_1 (
    .in0(adder_1_out), .in1(subtractor_1_out), .in2(and_1_out), .in3(or_1_out), .in4(xor_1_out),
    .in7(multiplexer_2_out), .out(Alu_result), .sel(Alu_Op));  // open: in5, in6, en
  Multiplexer #(.select(3), .width(16)) multiplexer_2 (
    .in0(not_1_out), .in1(Right), .in2(adder_2_out), .in3(subtractor_2_out), .out(multiplexer_2_out),
    .sel(scr1));  // open: in4, in5, in6, in7, en
  // Probe on multiplexer_2_out
  Comparator #(.width(16), .mode("unsigned")) comparator_1 (
    .a(Alu_result), .b({16{1'b0}}), .eq(comparator_1_eq));  // open: gt, lt
  Register #(.width(1)) register_1 (.D(comparator_1_eq), .en(zfld), .Q(ZF), .clk(clk));  // open: clr
endmodule

module _4bit_register (
  input  Clock,
  input  WE,
  input  [3:0] Input,
  output [3:0] Output
);

  D_Flip_Flop d_ff_1 (.clk(Clock), .D(Input[0]), .Q(Output[0]), .en(WE));  // open: Qn, preset, reset
  D_Flip_Flop d_ff_2 (.clk(Clock), .D(Input[1]), .Q(Output[1]), .en(WE));  // open: Qn, preset, reset
  D_Flip_Flop d_ff_3 (.clk(Clock), .D(Input[2]), .Q(Output[2]), .en(WE));  // open: Qn, preset, reset
  D_Flip_Flop d_ff_4 (.clk(Clock), .D(Input[3]), .Q(Output[3]), .en(WE));  // open: Qn, preset, reset
endmodule

// PC
module _10bit_Register (
  input  Clock,
  input  WE,
  input  [9:0] Input,
  output [9:0] Output
);

  D_Flip_Flop d_ff_1 (.clk(Clock), .D(Input[0]), .Q(Output[0]), .en(WE));  // open: Qn, preset, reset
  D_Flip_Flop d_ff_2 (.clk(Clock), .D(Input[1]), .Q(Output[1]), .en(WE));  // open: Qn, preset, reset
  D_Flip_Flop d_ff_3 (.clk(Clock), .D(Input[2]), .Q(Output[2]), .en(WE));  // open: Qn, preset, reset
  D_Flip_Flop d_ff_4 (.clk(Clock), .D(Input[3]), .Q(Output[3]), .en(WE));  // open: Qn, preset, reset
  D_Flip_Flop d_ff_5 (.clk(Clock), .D(Input[4]), .Q(Output[4]), .en(WE));  // open: Qn, preset, reset
  D_Flip_Flop d_ff_6 (.clk(Clock), .D(Input[5]), .Q(Output[5]), .en(WE));  // open: Qn, preset, reset
  D_Flip_Flop d_ff_7 (.clk(Clock), .D(Input[6]), .Q(Output[6]), .en(WE));  // open: Qn, preset, reset
  D_Flip_Flop d_ff_8 (.clk(Clock), .D(Input[7]), .Q(Output[7]), .en(WE));  // open: Qn, preset, reset
  D_Flip_Flop d_ff_9 (.clk(Clock), .D(Input[8]), .Q(Output[8]), .en(WE));  // open: Qn, preset, reset
  D_Flip_Flop d_ff_10 (.clk(Clock), .D(Input[9]), .Q(Output[9]), .en(WE));  // open: Qn, preset, reset
endmodule

// CPU
module Control_Unit (
  input  [3:0] opcode,
  input  ZF,
  input  Clock,
  output DATAMUX,
  output PCMUX,
  output SPDEC,
  output SPINC,
  output ZFLD,
  output MEMLD,
  output REGLD,
  output IRLD,
  output PCINC,
  output PCLD,
  output ADRMUX1,
  output ADRMUX2,
  output MUX
);

  wire not_1_out, not_2_out;
  wire [1:1] and_1_out;
  wire [3:0] multiplexer_1_out, multiplexer_2_out, n4bit_register_1_output, rom_1_data;
  wire [17:17] rom_1_data_2;

  and and_1 (and_1_out[1], opcode[0], not_1_out, opcode[2], not_2_out);
  not not_1 (not_1_out, opcode[1]);
  not not_2 (not_2_out, opcode[3]);
  Multiplexer #(.width(4)) multiplexer_1 (
    .in0(rom_1_data), .in1(multiplexer_2_out), .out(multiplexer_1_out), .sel(rom_1_data_2[17]));  // open: en
  _4bit_register u_4bit_register_1 (
    .Clock(Clock), .WE(1'b1), .Input(multiplexer_1_out), .Output(n4bit_register_1_output));
  Multiplexer #(.select(2), .width(4)) multiplexer_2 (
    .in0(opcode), .in1(opcode), .in2(4'b0000), .in3(4'b0100), .out(multiplexer_2_out),
    .sel({and_1_out[1], ZF}));  // open: en
  ROM #(.addrWidth(4), .dataWidth(18)) rom_1 (
    .addr(n4bit_register_1_output),
    .data({rom_1_data_2[17], MUX, ADRMUX2, ADRMUX1, PCLD, PCINC, IRLD, REGLD, MEMLD, ZFLD, SPINC, SPDEC, PCMUX, DATAMUX, rom_1_data}));  // open: sel
  // Probe on rom_1_data

  // Notes on the sheet:
  //   contents of rom_1 (hex, n*v repeats v):
  //   21800 1400 4400 4200 2000 0 0 10500 8240 9c a250 8d 8400 a0a0
endmodule

module CPU (
  input  [15:0] Data_IN,
  input  Clock,
  output [15:0] Data_OUT,
  output MEMWRT,
  output [11:0] ADDR
);

  wire DATAMUX, IRLD, MUX, PCINC, PCLD, PCMUX, REGLD, SPDEC, SPINC, ZF, ZFLD;
  wire [1:0] ADRMUX;
  wire [2:0] aluop, dest, src1, src2;
  wire [11:0] adder_1_out, multiplexer_2_out, multiplexer_4_out, pc_1_pc;
  wire [15:0] alu_1_alu_result, bit_extender_1_out, SP_ADDR, src1_out, src2_out;
  wire [15:12] multiplexer_4_out_2, n16bit_register_1_output;

  Control_Unit control_unit_1 (
    .DATAMUX(DATAMUX), .PCMUX(PCMUX), .SPDEC(SPDEC), .SPINC(SPINC), .ZFLD(ZFLD), .MEMLD(MEMWRT),
    .REGLD(REGLD), .IRLD(IRLD), .PCINC(PCINC), .PCLD(PCLD), .ADRMUX1(ADRMUX[0]), .ADRMUX2(ADRMUX[1]),
    .MUX(MUX), .opcode(Data_IN[15:12]), .Clock(Clock), .ZF(ZF));
  PC pc_1 (.pcinc(PCINC), .ADDR(multiplexer_2_out), .clk(Clock), .pcld(PCLD), .PC(pc_1_pc));
  Multiplexer #(.select(2), .width(12)) multiplexer_1 (
    .in0(pc_1_pc), .in1(src2_out[11:0]), .in2(SP_ADDR[11:0]), .in3({12{1'b0}}), .out(ADDR), .sel(ADRMUX));  // open: en
  Multiplexer #(.width(12)) multiplexer_2 (
    .in0(adder_1_out), .in1(multiplexer_4_out), .out(multiplexer_2_out), .sel(PCMUX));  // open: en
  Adder #(.width(12)) adder_1 (.a({aluop, src1, src2, dest}), .b(pc_1_pc), .out(adder_1_out));  // open: cin, cout
  Multiplexer #(.width(16)) multiplexer_3 (
    .in0(src1_out), .in1(bit_extender_1_out), .out(Data_OUT), .sel(DATAMUX));  // open: en
  assign bit_extender_1_out = {{4{1'b0}}, pc_1_pc};  // Bit_Extender bit_extender_1
  Multiplexer #(.width(16)) multiplexer_4 (
    .in0(Data_IN), .in1(alu_1_alu_result), .out({multiplexer_4_out_2, multiplexer_4_out}), .sel(MUX));  // open: en
  Regbank regbank_1 (
    .Data_in({multiplexer_4_out_2, multiplexer_4_out}), .Data_Address(dest), .Load(REGLD),
    .Source1_Out(src1_out), .Source2_Out(src2_out), .Source1(src1), .Source2(src2), .spinc(SPINC),
    .spdec(SPDEC), .SP_ADDR(SP_ADDR), .clk(Clock));
  // Probe on src2_out
  ALU alu_1 (
    .Left(src1_out), .Right(src2_out), .scr1(src1), .Alu_Op(aluop), .zfld(ZFLD), .clk(Clock), .ZF(ZF),
    .Alu_result(alu_1_alu_result));
  // Probe on src1_out
  _16bit_Register u_16bit_register_1 (
    .Clock(Clock), .WE(IRLD), .Input(Data_IN), .Output({n16bit_register_1_output, aluop, src1, src2, dest}));

  // Other names for the same wires on the sheet: clk = Clock; opcode[3:0] = Data_IN[15:12]; MEMLD = MEMWRT
endmodule

module PC (
  input  pcinc,
  input  [11:0] ADDR,
  input  clk,
  input  pcld,
  output [11:0] PC
);

  wire [11:0] adder_1_out, multiplexer_1_out, multiplexer_2_out;

  Adder #(.width(12)) adder_1 (.a(PC), .b(12'h1), .out(adder_1_out));  // open: cin, cout
  Multiplexer #(.width(12)) multiplexer_1 (
    .in0(PC), .in1(adder_1_out), .out(multiplexer_1_out), .sel(pcinc));  // open: en
  Multiplexer #(.width(12)) multiplexer_2 (
    .in0(multiplexer_1_out), .in1(ADDR), .out(multiplexer_2_out), .sel(pcld));  // open: en
  Register #(.width(12)) PC_REG (.D(multiplexer_2_out), .en(1'b1), .Q(PC), .clk(clk));  // open: clr
endmodule

module main (
  input  [15:0] READY_BUTTON,
  input  ReadyBit
);

  wire _7Seg_LD, clk, InputSignal, MEM_LD, memwrt, Status;
  wire [3:0] n7_seg_reg_1__1hex, n7_seg_reg_1__2hex, n7_seg_reg_1__3hex, n7_seg_reg_1__4hex;
  wire [9:0] MEM_ADDR;
  wire [11:0] ADDR;
  wire [15:0] DATA_IN, DATA_IN_MEM, DATA_OUT, I_O_Data;

  Clock clock_1 (.out(clk));
  I_O_Controller i_o_controller_1 (
    .DIP_SWITCH(READY_BUTTON), .ReadyBit(ReadyBit), .clk(clk), .Data_Out(I_O_Data), .Status(Status),
    .AND_Gate(InputSignal));
  Address_Decoder address_decoder_1 (
    .I_O_Data(I_O_Data), .memwrt(memwrt), .ADDR(ADDR), .DATA_IN_MEM(DATA_IN_MEM), .MEM_LD(MEM_LD),
    ._7Seg_LD(_7Seg_LD), .InputSignal(InputSignal), .Status(Status), .MEM_ADDR(MEM_ADDR), .DATA_IN(DATA_IN));
  RAM #(.addrWidth(10), .dataWidth(16), .bus("separate")) ram_1 (
    .addr(MEM_ADDR), .din(DATA_OUT), .data(DATA_IN_MEM), .str(MEM_LD), .clk(clk));  // open: sel, ld, clr
  CPU cpu_1 (.Clock(clk), .Data_IN(DATA_IN), .Data_OUT(DATA_OUT), .MEMWRT(memwrt), .ADDR(ADDR));
  Hex_Digit_Display hex_digit_display_1 (.value(n7_seg_reg_1__4hex));  // open: dp
  Hex_Digit_Display hex_digit_display_2 (.value(n7_seg_reg_1__3hex));  // open: dp
  _7_Seg_Reg u_7_seg_reg_1 (
    .clk(clk), .LD(_7Seg_LD), .DATA_IN(DATA_OUT), ._4hex(n7_seg_reg_1__4hex), ._3hex(n7_seg_reg_1__3hex),
    ._2hex(n7_seg_reg_1__2hex), ._1hex(n7_seg_reg_1__1hex));
  Hex_Digit_Display hex_digit_display_3 (.value(n7_seg_reg_1__1hex));  // open: dp
  Hex_Digit_Display hex_digit_display_4 (.value(n7_seg_reg_1__2hex));  // open: dp
endmodule

// 7-Seg
module _7_Seg_Reg (
  input  clk,
  input  LD,
  input  [15:0] DATA_IN,
  output [3:0] _4hex,
  output [3:0] _3hex,
  output [3:0] _2hex,
  output [3:0] _1hex
);

  Register #(.width(4)) register_1 (.D(DATA_IN[15:12]), .en(LD), .Q(_4hex), .clk(clk));  // open: clr
  Register #(.width(4)) register_2 (.D(DATA_IN[11:8]), .en(LD), .Q(_3hex), .clk(clk));  // open: clr
  Register #(.width(4)) register_3 (.D(DATA_IN[7:4]), .en(LD), .Q(_2hex), .clk(clk));  // open: clr
  Register #(.width(4)) register_4 (.D(DATA_IN[3:0]), .en(LD), .Q(_1hex), .clk(clk));  // open: clr
endmodule

// ext
module ext_ready (
  input  ReadyBit,
  output [15:0] Ready_Out
);


  assign Ready_Out = {{13{1'b0}}, ReadyBit, 2'b00};
endmodule

module Address_Decoder (
  input  [15:0] DATA_IN_MEM,
  input  [15:0] I_O_Data,
  input  memwrt,
  input  [11:0] ADDR,
  output [15:0] DATA_IN,
  output MEM_LD,
  output _7Seg_LD,
  output InputSignal,
  output Status,
  output [9:0] MEM_ADDR
);

  wire _7Seg_CATCH, MEM_CATCH;
  wire [1:0] priority_encoder_1_out;

  and MEM (MEM_CATCH, ~ADDR[11], ~ADDR[10]);  // AND_Gate
  and F00 (InputSignal, ADDR[11], ADDR[10], ADDR[9], ADDR[8], ~ADDR[7], ~ADDR[6], ~ADDR[5], ~ADDR[4], ~ADDR[3], ~ADDR[2], ~ADDR[1], 1'b1);  // AND_Gate
  Priority_Encoder #(.select(2)) priority_encoder_1 (
    .in0(1'b1), .in1(MEM_CATCH), .in2(InputSignal), .in3(1'b0), .out(priority_encoder_1_out));
  and _500 (_7Seg_CATCH, ~ADDR[11], ADDR[10], ~ADDR[9], ADDR[8], ~ADDR[7], ~ADDR[6], ~ADDR[5], ~ADDR[4], ~ADDR[3], ~ADDR[2], ~ADDR[1], ~ADDR[0]);  // AND_Gate
  Multiplexer #(.select(2), .width(16)) multiplexer_1 (
    .in0({16{1'b0}}), .in1(DATA_IN_MEM), .in2(I_O_Data), .in3({16{1'b0}}), .out(DATA_IN),
    .sel(priority_encoder_1_out));  // open: en
  and and_1 (MEM_LD, memwrt, MEM_CATCH);
  and and_2 (_7Seg_LD, _7Seg_CATCH, memwrt);

  assign MEM_ADDR = ADDR[9:0];
  assign Status = ADDR[0];

  // Other names for the same wires on the sheet: DPS_CATCH = InputSignal
endmodule

// I/O Controller
module I_O_Controller (
  input  [15:0] DIP_SWITCH,
  input  ReadyBit,
  input  clk,
  input  Status,
  input  AND_Gate,
  output [15:0] Data_Out
);

  wire and_1_out, register_2_q;
  wire [15:0] ext_ready_1_ready_out, register_1_q;

  Register #(.width(16)) register_1 (.D(DIP_SWITCH), .en(1'b1), .Q(register_1_q), .clk(register_2_q));  // open: clr
  and and_1 (and_1_out, ~Status, AND_Gate);  // AND_Gate
  ext_ready ext_ready_1 (.ReadyBit(register_2_q), .Ready_Out(ext_ready_1_ready_out));
  Register #(.width(1)) register_2 (.D(ReadyBit), .Q(register_2_q), .clk(clk), .clr(and_1_out));  // open: en
  Multiplexer #(.width(16)) multiplexer_1 (
    .in0(register_1_q), .in1(ext_ready_1_ready_out), .out(Data_Out), .sel(Status));  // open: en
endmodule
