// Logisim project Logisim_Circuits.circ as structural Verilog: 7 circuits, main circuit main
module main (
  input  Clock
);

  wire control_unit_1_irld, control_unit_1_mux_signal, control_unit_1_pcinc_signal,
       control_unit_1_regld_signal;
  wire [1:0] n16bit_register_1_output, n16bit_register_1_output_2, n16bit_register_1_output_3;
  wire [3:0] n16bit_register_1_output_5;
  wire [9:0] adder_1_out, multiplexer_1_out, n10bit_register_1_output;
  wire [15:0] alu_1_alu_result, multiplexer_2_out, ram_1_data, regbank_1_address_a_out,
       regbank_1_address_b_out, regbank_1_r0_output;
  wire [15:2] n16bit_register_1_output_4;

  Multiplexer #(.width(10)) multiplexer_1 (
    .in0(n10bit_register_1_output), .in1(adder_1_out), .out(multiplexer_1_out),
    .sel(control_unit_1_pcinc_signal));  // open: en
  _10bit_Register u_10bit_register_1 (
    .Clock(Clock), .WE(1'b1), .Input(multiplexer_1_out), .Output(n10bit_register_1_output));
  RAM #(.addrWidth(10), .dataWidth(16), .bus("separate")) ram_1 (
    .addr(n10bit_register_1_output), .data(ram_1_data), .ld(1'b1));  // open: din, str, sel, clk, clr
  Adder #(.width(10)) adder_1 (.a(n10bit_register_1_output), .b(10'h1), .out(adder_1_out));  // open: cin, cout
  Hex_Digit_Display hex_digit_display_1 (.value(regbank_1_r0_output[11:8]));  // open: dp
  Hex_Digit_Display hex_digit_display_2 (.value(regbank_1_r0_output[15:12]));  // open: dp
  Hex_Digit_Display hex_digit_display_3 (.value(regbank_1_r0_output[3:0]));  // open: dp
  Hex_Digit_Display hex_digit_display_4 (.value(regbank_1_r0_output[7:4]));  // open: dp
  RegBank regbank_1 (
    .Data_in(multiplexer_2_out), .Data_Address(n16bit_register_1_output), .Load(control_unit_1_regld_signal),
    .Clock(Clock), .R0_Output(regbank_1_r0_output), .Address_A_Out(regbank_1_address_a_out),
    .Address_B_Out(regbank_1_address_b_out), .Address_A(n16bit_register_1_output_3),
    .Address_B(n16bit_register_1_output_2));
  Multiplexer #(.width(16)) multiplexer_2 (
    .in0(alu_1_alu_result), .in1(ram_1_data), .out(multiplexer_2_out), .sel(control_unit_1_mux_signal));  // open: en
  ALU alu_1 (
    .Left(regbank_1_address_a_out), .Right(regbank_1_address_b_out), .Alu_result(alu_1_alu_result),
    .Alu_Op(n16bit_register_1_output_5));
  Control_Unit control_unit_1 (
    .Opcode(ram_1_data[15:14]), .Clock(Clock), .Mux_Signal(control_unit_1_mux_signal),
    .RegLD_Signal(control_unit_1_regld_signal), .PCINC_Signal(control_unit_1_pcinc_signal),
    .IRLD(control_unit_1_irld));
  _16bit_Register u_16bit_register_1 (
    .Clock(Clock), .WE(control_unit_1_irld), .Input(ram_1_data),
    .Output({n16bit_register_1_output_4[15:12], n16bit_register_1_output_5, n16bit_register_1_output_3, n16bit_register_1_output_4[5], n16bit_register_1_output_2, n16bit_register_1_output_4[2], n16bit_register_1_output}));
endmodule

module RegBank (
  input  [15:0] Data_in,
  input  [1:0] Data_Address,
  input  Load,
  input  [1:0] Address_A,
  input  Clock,
  input  [1:0] Address_B,
  output [15:0] R0_Output,
  output [15:0] Address_A_Out,
  output [15:0] Address_B_Out
);

  wire and_1_out, and_2_out, and_3_out, and_4_out, decoder_1_out0, decoder_1_out1, decoder_1_out2,
       decoder_1_out3;
  wire [15:0] n16bit_register_2_output, n16bit_register_3_output, n16bit_register_4_output;

  Decoder #(.select(2)) decoder_1 (
    .out0(decoder_1_out0), .out1(decoder_1_out1), .out2(decoder_1_out2), .out3(decoder_1_out3),
    .sel(Data_Address));  // open: en
  and and_1 (and_1_out, Load, decoder_1_out0);
  and and_2 (and_2_out, Load, decoder_1_out1);
  and and_3 (and_3_out, Load, decoder_1_out2);
  and and_4 (and_4_out, Load, decoder_1_out3);
  _16bit_Register u_16bit_register_1 (.Clock(Clock), .WE(and_1_out), .Input(Data_in), .Output(R0_Output));
  _16bit_Register u_16bit_register_2 (
    .Clock(Clock), .WE(and_2_out), .Input(Data_in), .Output(n16bit_register_2_output));
  _16bit_Register u_16bit_register_3 (
    .Clock(Clock), .WE(and_3_out), .Input(Data_in), .Output(n16bit_register_3_output));
  _16bit_Register u_16bit_register_4 (
    .Clock(Clock), .WE(and_4_out), .Input(Data_in), .Output(n16bit_register_4_output));
  Multiplexer #(.select(2), .width(16)) multiplexer_1 (
    .in0(R0_Output), .in1(n16bit_register_2_output), .in2(n16bit_register_3_output),
    .in3(n16bit_register_4_output), .out(Address_A_Out), .sel(Address_A));  // open: en
  Multiplexer #(.select(2), .width(16)) multiplexer_2 (
    .in0(R0_Output), .in1(n16bit_register_2_output), .in2(n16bit_register_3_output),
    .in3(n16bit_register_4_output), .out(Address_B_Out), .sel(Address_B));  // open: en
endmodule

module ALU (
  input  [15:0] Left,
  input  [15:0] Right,
  input  [3:0] Alu_Op,
  output [15:0] Alu_result
);

  wire [15:0] adder_1_out, adder_2_out, and_1_out, not_1_out, or_1_out, subtractor_1_out, subtractor_2_out,
       xor_1_out;

  Adder #(.width(16)) adder_1 (.a(Left), .b(Right), .out(adder_1_out));  // open: cin, cout
  Subtractor #(.width(16)) subtractor_1 (.a(Left), .b(Right), .out(subtractor_1_out));  // open: bin, bout
  assign and_1_out = Left & Right;  // AND_Gate and_1, 16 bits wide
  assign or_1_out = Left | Right;  // OR_Gate or_1, 16 bits wide
  assign xor_1_out = Left ^ Right;  // XOR_Gate xor_1, 16 bits wide
  assign not_1_out = ~Right;  // NOT_Gate not_1, 16 bits wide
  Adder #(.width(16)) adder_2 (.a(16'h1), .b(Right), .out(adder_2_out));  // open: cin, cout
  Subtractor #(.width(16)) subtractor_2 (.a(Right), .b(16'h1), .out(subtractor_2_out));  // open: bin, bout
  Multiplexer #(.select(4), .width(16)) multiplexer_1 (
    .in0(adder_1_out), .in1(subtractor_1_out), .in2(and_1_out), .in3(or_1_out), .in4(xor_1_out),
    .in5(not_1_out), .in6(Right), .in7(adder_2_out), .in8(subtractor_2_out), .in9({16{1'b0}}),
    .out(Alu_result), .sel(Alu_Op));  // open: in10, in11, in12, in13, in14, in15, en
endmodule

// IR
module _16bit_Register (
  input  Clock,
  input  WE,
  input  [15:0] Input,
  output [15:0] Output
);

  D_Flip_Flop d_ff_1 (.clk(Clock), .D(Input[0]), .Q(Output[0]), .en(WE));  // open: Qn, preset, reset
  D_Flip_Flop d_ff_2 (.clk(Clock), .D(Input[1]), .Q(Output[1]), .en(WE));  // open: Qn, preset, reset
  D_Flip_Flop d_ff_3 (.clk(Clock), .D(Input[2]), .Q(Output[2]), .en(WE));  // open: Qn, preset, reset
  D_Flip_Flop d_ff_4 (.clk(Clock), .D(Input[3]), .Q(Output[3]), .en(WE));  // open: Qn, preset, reset
  D_Flip_Flop d_ff_5 (.clk(Clock), .D(Input[4]), .Q(Output[4]), .en(WE));  // open: Qn, preset, reset
  D_Flip_Flop d_ff_6 (.clk(Clock), .D(Input[5]), .Q(Output[5]), .en(WE));  // open: Qn, preset, reset
  D_Flip_Flop d_ff_7 (.clk(Clock), .D(Input[6]), .Q(Output[6]), .en(WE));  // open: Qn, preset, reset
  D_Flip_Flop d_ff_8 (.clk(Clock), .D(Input[7]), .Q(Output[7]), .en(WE));  // open: Qn, preset, reset
  D_Flip_Flop d_ff_9 (.clk(Clock), .D(Input[8]), .Q(Output[8]), .en(WE));  // open: Qn, preset, reset
  D_Flip_Flop d_ff_10 (.clk(Clock), .D(Input[9]), .Q(Output[9]), .en(WE));  // open: Qn, preset, reset
  D_Flip_Flop d_ff_11 (.clk(Clock), .D(Input[10]), .Q(Output[10]), .en(WE));  // open: Qn, preset, reset
  D_Flip_Flop d_ff_12 (.clk(Clock), .D(Input[11]), .Q(Output[11]), .en(WE));  // open: Qn, preset, reset
  D_Flip_Flop d_ff_13 (.clk(Clock), .D(Input[12]), .Q(Output[12]), .en(WE));  // open: Qn, preset, reset
  D_Flip_Flop d_ff_14 (.clk(Clock), .D(Input[13]), .Q(Output[13]), .en(WE));  // open: Qn, preset, reset
  D_Flip_Flop d_ff_15 (.clk(Clock), .D(Input[14]), .Q(Output[14]), .en(WE));  // open: Qn, preset, reset
  D_Flip_Flop d_ff_16 (.clk(Clock), .D(Input[15]), .Q(Output[15]), .en(WE));  // open: Qn, preset, reset
endmodule

// PC
module _10bit_Register (
  input  Clock,
  input  WE,
  input  [9:0] Input,
  output [9:0] Output
);

  D_Flip_Flop d_ff_1 (.clk(Clock), .D(Input[0]), .Q(Output[0]), .en(WE));  // open: Qn, preset, reset
  D_Flip_Flop d_ff_2 (.clk(Clock), .D(Input[1]), .Q(Output[1]), .en(WE));  // open: Qn, preset, reset
  D_Flip_Flop d_ff_3 (.clk(Clock), .D(Input[2]), .Q(Output[2]), .en(WE));  // open: Qn, preset, reset
  D_Flip_Flop d_ff_4 (.clk(Clock), .D(Input[3]), .Q(Output[3]), .en(WE));  // open: Qn, preset, reset
  D_Flip_Flop d_ff_5 (.clk(Clock), .D(Input[4]), .Q(Output[4]), .en(WE));  // open: Qn, preset, reset
  D_Flip_Flop d_ff_6 (.clk(Clock), .D(Input[5]), .Q(Output[5]), .en(WE));  // open: Qn, preset, reset
  D_Flip_Flop d_ff_7 (.clk(Clock), .D(Input[6]), .Q(Output[6]), .en(WE));  // open: Qn, preset, reset
  D_Flip_Flop d_ff_8 (.clk(Clock), .D(Input[7]), .Q(Output[7]), .en(WE));  // open: Qn, preset, reset
  D_Flip_Flop d_ff_9 (.clk(Clock), .D(Input[8]), .Q(Output[8]), .en(WE));  // open: Qn, preset, reset
  D_Flip_Flop d_ff_10 (.clk(Clock), .D(Input[9]), .Q(Output[9]), .en(WE));  // open: Qn, preset, reset
endmodule

// Control Unit
module Control_Unit (
  input  [1:0] Opcode,
  input  Clock,
  output Mux_Signal,
  output RegLD_Signal,
  output PCINC_Signal,
  output IRLD
);

  wire [1:0] multiplexer_1_out, n2bit_register_1_output;
  wire [7:4] rom_1_data;

  Multiplexer #(.width(2)) multiplexer_1 (
    .in0(Opcode), .in1(2'b00), .out(multiplexer_1_out), .sel(rom_1_data[4]));  // open: en
  _2bit_Register u_2bit_register_1 (
    .Clock(Clock), .WE(1'b1), .Input(multiplexer_1_out), .Output(n2bit_register_1_output));
  ROM #(.addrWidth(2)) rom_1 (
    .addr(n2bit_register_1_output), .data({rom_1_data, IRLD, PCINC_Signal, RegLD_Signal, Mux_Signal}));  // open: sel

  // Notes on the sheet:
  //   contents of rom_1 (hex, n*v repeats v):
  //   c 17 12
endmodule

module _2bit_Register (
  input  Clock,
  input  WE,
  input  [1:0] Input,
  output [1:0] Output
);

  D_Flip_Flop d_ff_1 (.clk(Clock), .D(Input[0]), .Q(Output[0]), .en(WE));  // open: Qn, preset, reset
  D_Flip_Flop d_ff_2 (.clk(Clock), .D(Input[1]), .Q(Output[1]), .en(WE));  // open: Qn, preset, reset
endmodule
